// Logisim project ex5.circ as structural Verilog: 5 circuits, main circuit rotr
module rotr (
  input  [15:0] A,
  input  [3:0] B,
  output [15:0] Out1
);

  wire [15:0] rot1_1_out_2, rot2_1_out_2, rot4_1_out_2, rot8_1_out_2, step1, step2, step4;

  rot2 rot2_1 (.in_1(step1), .out_2(rot2_1_out_2));
  rot4 rot4_1 (.in_1(step2), .out_2(rot4_1_out_2));
  rot8 rot8_1 (.in_1(step4), .out_2(rot8_1_out_2));
  Multiplexer #(.width(16), .enable("false")) multiplexer_1 (.in0(step1), .in1(rot2_1_out_2), .out(step2), .sel(B[1]));
  Multiplexer #(.width(16), .enable("false")) multiplexer_2 (.in0(step2), .in1(rot4_1_out_2), .out(step4), .sel(B[2]));
  Multiplexer #(.width(16), .enable("false")) multiplexer_3 (.in0(step4), .in1(rot8_1_out_2), .out(Out1), .sel(B[3]));
  rot1 rot1_1 (.in_1(A), .out_2(rot1_1_out_2));
  Multiplexer #(.width(16), .enable("false")) multiplexer_4 (.in0(A), .in1(rot1_1_out_2), .out(step1), .sel(B[0]));

  // Other names for the same wires on the sheet: ans[15:0] = Out1; t1 = B[0]; t2 = B[1]; t3 = B[2]; t4 = B[3]

  // Notes on the sheet:
  //   PUT CIRCUITRY HERE
endmodule

module rot8 (
  input  [15:0] in_1,
  output [15:0] out_2
);

  wire [15:0] rot4_1_out_2;

  rot4 rot4_1 (.in_1(in_1), .out_2(rot4_1_out_2));
  rot4 rot4_2 (.in_1(rot4_1_out_2), .out_2(out_2));

  // Notes on the sheet:
  //   PUT CIRCUITRY HERE
endmodule

module rot4 (
  input  [15:0] in_1,
  output [15:0] out_2
);

  wire [15:0] rot2_1_out_2;

  rot2 rot2_1 (.in_1(in_1), .out_2(rot2_1_out_2));
  rot2 rot2_2 (.in_1(rot2_1_out_2), .out_2(out_2));

  // Notes on the sheet:
  //   PUT CIRCUITRY HERE
endmodule

module rot2 (
  input  [15:0] in_1,
  output [15:0] out_2
);

  wire [15:0] rot1_1_out_2;

  rot1 rot1_1 (.in_1(in_1), .out_2(rot1_1_out_2));
  rot1 rot1_2 (.in_1(rot1_1_out_2), .out_2(out_2));

  // Notes on the sheet:
  //   PUT CIRCUITRY HERE
endmodule

module rot1 (
  input  [15:0] in_1,
  output [15:0] out_2
);


  assign out_2 = {in_1[0], in_1[15:1]};

  // Other names for the same wires on the sheet: t1[14:0] = in_1[15:1]; t2 = in_1[0]

  // Notes on the sheet:
  //   PUT CIRCUITRY HERE
endmodule
