// Logisim project alu.circ as structural Verilog: 8 circuits, main circuit alu
module alu (
  input  [31:0] A,
  input  [31:0] B,
  input  [3:0] ALUSel,
  output [31:0] Result
);

  wire [31:0] ADD3, AND0, DIV9, DIVU8, MULH7, MULHU6, MULT5, OR1, REMU10, SIR14, SLL15, SLT13, SRA12, SRL11,
       SUB4, XOR2;

  assign AND0 = A & B;  // AND_Gate and_1, 32 bits wide
  Subtractor #(.width(32)) subtractor_1 (.a(A), .b(B), .out(SUB4));  // open: bin, bout
  Divider #(.width(32)) divider_1 (.a(A), .b(B), .out(DIVU8));  // open: upper, rem
  sra1 sra1_1 (.A(A), .B(B), .RESULT(SRA12));
  assign OR1 = A | B;  // OR_Gate or_1, 32 bits wide
  Multiplier #(.width(32)) multiplier_1 (.a(A), .b(B), .out(MULT5));  // open: cin, cout
  div div_1 (.in_1(A), .in_2(B), .out_3(DIV9));
  slt slt_1 (.A(A), .B(B), .RESULT(SLT13));
  Multiplexer #(.select(4), .width(32), .enable("false")) multiplexer_1 (
    .in0(AND0), .in1(OR1), .in2(XOR2), .in3(ADD3), .in4(SUB4), .in5(MULT5), .in6(MULHU6), .in7(MULH7),
    .in8(DIVU8), .in9(DIV9), .in10(REMU10), .in11(SRL11), .in12(SRA12), .in13(SLT13), .in14(SIR14),
    .in15(SLL15), .out(Result), .sel(ALUSel));
  assign XOR2 = A ^ B;  // XOR_Gate xor_1, 32 bits wide
  Multiplier #(.width(32)) multiplier_2 (.a(A), .b(B), .cout(MULHU6));  // open: out, cin
  Divider #(.width(32)) divider_2 (.a(A), .b(B), .rem(REMU10));  // open: out, upper
  sir sir_1 (.A(A), .B(B), .RESULT(SIR14));
  Adder #(.width(32)) adder_1 (.a(A), .b(B), .out(ADD3));  // open: cin, cout
  mulh mulh_1 (.in_1(A), .in_2(B), .out_3(MULH7));
  srl1 srl1_1 (.A(A), .B(B), .RESULT(SRL11));
  sll1 sll1_1 (.RESULT(SLL15), .A(A), .B(B));

  // Notes on the sheet:
  //   INPUTS to your circuit
  //   12:SRA
  //   0: AND
  //   4: SUB
  //   8:DIVU
  //   1: OR
  //   5:MULT
  //   9:DIV
  //   13:SLT
  //   MUX from ALUSel
  //   DON'T CHANGE THE LOCATIONS OF THE INPUTS AND OUTPUTS!
  //   2: XOR
  //   6:MULHU
  //   10:REMU
  //   14:SIR
  //   OUTPUT from your circuit
  //   3: ADD
  //   7: MULH
  //   11: SRL
  //   15: CNTO
endmodule

module srl1 (
  input  [31:0] A,
  input  [31:0] B,
  output [31:0] RESULT
);

  Shifter #(.width(32), .shift("lr")) shifter_1 (.in(A), .\dist (B[4:0]), .out(RESULT));
endmodule

module slt (
  input  [31:0] A,
  input  [31:0] B,
  output [31:0] RESULT
);

  Comparator #(.width(32)) comparator_1 (.a(A), .b(B), .lt(RESULT[0]));  // open: gt, eq

  assign RESULT[31:1] = {31{1'b0}};
endmodule

module mulh (
  input  [31:0] in_1,
  input  [31:0] in_2,
  output [31:0] out_3
);

  wire [31:0] A_N_B_P, A_P_B_N, both_N, both_P;

  Multiplier #(.width(32)) multiplier_1 (.a(in_1), .b(in_2), .cout(both_P));  // open: out, cin
  Subtractor #(.width(32)) subtractor_1 (.a(both_P), .b({1'b0, in_2[30:0]}), .out(A_N_B_P));  // open: bin, bout
  Multiplexer #(.select(2), .width(32), .enable("false")) multiplexer_1 (
    .in0(both_P), .in1(A_N_B_P), .in2(A_P_B_N), .in3(both_N), .out(out_3), .sel({in_2[31], in_1[31]}));
  Subtractor #(.width(32)) subtractor_2 (.a(both_P), .b({1'b0, in_1[30:0]}), .out(A_P_B_N));  // open: bin, bout
  Subtractor #(.width(32)) subtractor_3 (.a(A_N_B_P), .b({1'b0, in_1[30:0]}), .out(both_N));  // open: bin, bout

  // Other names for the same wires on the sheet: A[31:0] = in_1; A_31[30:0] = in_1[30:0]; B[31:0] = in_2;
  //   B_31[30:0] = in_2[30:0]; judger[1:0] = {in_2[31], in_1[31]}; result[31:0] = out_3
endmodule

module sir (
  input  [31:0] A,
  input  [31:0] B,
  output [31:0] RESULT
);

  Comparator #(.width(32)) comparator_1 (
    .a(A),
    .b({B[0], B[1], B[2], B[3], B[4], B[5], B[6], B[7], B[8], B[9], B[10], B[11], B[12], B[13], B[14], B[15], B[16], B[17], B[18], B[19], B[20], B[21], B[22], B[23], B[24], B[25], B[26], B[27], B[28], B[29], B[30], B[31]}),
    .eq(RESULT[0]));  // open: gt, lt

  assign RESULT[31:1] = {31{1'b0}};

  // Other names for the same wires on the sheet: Bturn[31:0] = {B[0], B[1], B[2], B[3], B[4], B[5], B[6], B[7], B[8], B[9], B[10], B[11], B[12], B[13], B[14], B[15], B[16], B[17], B[18], B[19], B[20], B[21], B[22], B[23], B[24], B[25], B[26], B[27], B[28], B[29], B[30], B[31]}

  // Notes on the sheet:
  //   turn step
  //   judge step
endmodule

module sra1 (
  input  [31:0] A,
  input  [31:0] B,
  output [31:0] RESULT
);

  wire check0, check32, comparator_1_gt, comparator_2_lt;
  wire [4:0] Bshift;
  wire [31:0] Ashift, negator_1_out, shifter_1_out, shifter_2_out;
  wire [31:5] multiplexer_2_out;

  // Probe on A
  // Probe on Bshift
  Comparator #(.width(32)) comparator_1 (.a(B), .b(32'h1f), .gt(comparator_1_gt));  // open: eq, lt
  Comparator #(.width(32)) comparator_2 (.a(B), .b(32'hffffffe1), .lt(comparator_2_lt));  // open: gt, eq
  Shifter #(.width(32), .shift("lr")) shifter_1 (.in(A), .\dist (Bshift), .out(shifter_1_out));
  Shifter #(.width(32)) shifter_2 (.in(A), .\dist (Bshift), .out(shifter_2_out));
  // Probe on Ashift
  Multiplexer #(.width(32), .enable("false")) multiplexer_1 (
    .in0(shifter_1_out), .in1(shifter_2_out), .out(Ashift), .sel(check0));
  or or_1 (check32, comparator_1_gt, comparator_2_lt);
  // Probe on check32
  Negator #(.width(32)) negator_1 (.in(B), .out(negator_1_out));
  Comparator #(.width(32)) comparator_3 (.a(B), .b({32{1'b0}}), .lt(check0));  // open: gt, eq
  Multiplexer #(.width(32), .enable("false")) multiplexer_2 (
    .in0(B), .in1(negator_1_out), .out({multiplexer_2_out, Bshift}), .sel(check0));
  Multiplexer #(.width(32), .enable("false")) multiplexer_3 (
    .in0(Ashift), .in1({32{1'b0}}), .out(RESULT), .sel(check32));

  // Notes on the sheet:
  //   final check
endmodule

module sll1 (
  input  [31:0] A,
  input  [31:0] B,
  output [31:0] RESULT
);

  Shifter #(.width(32)) shifter_1 (.in(A), .\dist (B[4:0]), .out(RESULT));
endmodule

module div (
  input  [31:0] in_1,
  input  [31:0] in_2,
  output [31:0] out_3
);

  wire [31:0] A_N, A_N_B_P, A_P_B_N, B_N, both_N, both_P, divider_2_out, divider_3_out;

  // Probe on in_1
  // Probe on in_2
  Divider #(.width(32)) divider_1 (.a(in_1), .b(in_2), .out(both_P));  // open: upper, rem
  // Probe on A_N
  Negator #(.width(32)) negator_1 (.in(in_1), .out(A_N));
  // Probe on A_N
  Negator #(.width(32)) negator_2 (.in(in_2), .out(B_N));
  // Probe on out_3
  Divider #(.width(32)) divider_2 (.a(A_N), .b(in_2), .out(divider_2_out));  // open: upper, rem
  Negator #(.width(32)) negator_3 (.in(divider_2_out), .out(A_N_B_P));
  Multiplexer #(.select(2), .width(32), .enable("false")) multiplexer_1 (
    .in0(both_P), .in1(A_N_B_P), .in2(A_P_B_N), .in3(both_N), .out(out_3), .sel({in_2[31], in_1[31]}));
  Divider #(.width(32)) divider_3 (.a(in_1), .b(B_N), .out(divider_3_out));  // open: upper, rem
  Negator #(.width(32)) negator_4 (.in(divider_3_out), .out(A_P_B_N));
  Divider #(.width(32)) divider_4 (.a(A_N), .b(B_N), .out(both_N));  // open: upper, rem

  // Other names for the same wires on the sheet: A[31:0] = in_1; B[31:0] = in_2; judger[1:0] = {in_2[31], in_1[31]};
  //   result[31:0] = out_3
endmodule
