// Logisim project cpu.circ as structural Verilog: 5 circuits, main circuit main
module main (
  input  [31:0] INSTRUCTION,
  input  CLOCK,
  output [31:0] FETCH_ADDRESS,
  output [31:0] ra,
  output [31:0] sp,
  output [31:0] t0,
  output [31:0] t1,
  output [31:0] t2,
  output [31:0] s0,
  output [31:0] s1,
  output [31:0] a0
);

  wire ASel, BrEq, BrLt, BrUn, BSel, MemRW, PCSel, RegWEn;
  wire [1:0] WBSel;
  wire [2:0] func3, ImmSel, LoadSel;
  wire [3:0] ALUSel;
  wire [6:0] func7;
  wire [24:0] INST;
  wire [31:0] adder_1_out, adder_2_out, ALUResult, divider_2_out, fetch_addr2, Imm, multiplexer_1_out,
       multiplexer_2_out, multiplexer_3_out, multiplexer_5_out, PC_q, r1, r2, ReadData, ReadDataTrans,
       WB_data;

  Adder #(.width(32)) adder_1 (.a(PC_q), .b(32'h4), .out(adder_1_out));  // open: cin, cout
  Multiplexer #(.width(32), .enable("false")) multiplexer_1 (
    .in0(adder_1_out), .in1(ALUResult), .out(multiplexer_1_out), .sel(PCSel));
  Multiplexer #(.width(32), .enable("false")) multiplexer_2 (
    .in0(INSTRUCTION), .in1(32'h13), .out(multiplexer_2_out), .sel(PCSel));
  Register #(.width(32)) PC (.D(multiplexer_1_out), .clk(CLOCK), .Q(PC_q));  // open: en, clr
  Register #(.width(32)) register_1 (
    .D(multiplexer_2_out), .clk(CLOCK), .Q({func7, INST[24:15], func3, INST[11:0]}));  // open: en, clr
  // Probe on PC_q
  Register #(.width(32)) register_2 (.D(PC_q), .clk(CLOCK), .Q(fetch_addr2));  // open: en, clr
  // Probe on {func7, INST[24:15], func3, INST[11:0]}
  Divider #(.width(32)) divider_1 (.a(PC_q), .b(32'h4), .out(FETCH_ADDRESS));  // open: upper, rem
  control control_1 (
    .Instruction({func7, INST[24:15], func3, INST[11:0]}), .BrEq(BrEq), .BrLt(BrLt), .PCSel(PCSel),
    .RegWEn(RegWEn), .ImmSel(ImmSel), .BrUn(BrUn), .ASel(ASel), .BSel(BSel), .ALUSel(ALUSel), .MemRW(MemRW),
    .WBSel(WBSel), .LoadSel(LoadSel));
  // Probe on fetch_addr2
  // Probe on INST[24:20]
  Adder #(.width(32)) adder_2 (.a(fetch_addr2), .b(32'h4), .out(adder_2_out));  // open: cin, cout
  regfile_main RegFile (
    .rs2(INST[24:20]), .rd(INST[11:7]), .Read_Data_1(r1), .Read_Data_2(r2), .ra(ra), .sp(sp), .t0(t0),
    .t1(t1), .t2(t2), .s0(s0), .s1(s1), .a0(a0), .rs1(INST[19:15]), .Write_Data(WB_data), .RegWEn(RegWEn),
    .clk(CLOCK));
  branchCompare branchcompare_1 (.BrUn(BrUn), .rs1(r1), .rs2(r2), .BrEq(BrEq), .BrLt(BrLt));
  Multiplexer #(.width(32), .enable("false")) multiplexer_3 (.in0(r2), .in1(Imm), .out(multiplexer_3_out), .sel(BSel));
  // Probe on WB_data
  Multiplexer #(.select(2), .width(32), .enable("false")) multiplexer_4 (
    .in0(ReadDataTrans), .in1(ALUResult), .in2(adder_2_out), .in3(Imm), .out(WB_data), .sel(WBSel));
  Multiplexer #(.width(32), .enable("false")) multiplexer_5 (
    .in0(r1), .in1(fetch_addr2), .out(multiplexer_5_out), .sel(ASel));
  Divider #(.width(32)) divider_2 (.a(ALUResult), .b(32'h4), .out(divider_2_out));  // open: upper, rem
  // Probe on ALUResult
  alu Arithmetic_Logic_Unit (.A(multiplexer_5_out), .B(multiplexer_3_out), .ALUSel(ALUSel), .Result(ALUResult));
  mem_main DMEM (.WriteAddr(divider_2_out), .WriteData(r2), .MemRW(MemRW), .ReadData(ReadData), .clk(CLOCK));
  immGen immgen_1 (.Instruction({func7, INST[24:15], func3, INST[11:0]}), .ImmSel(ImmSel), .imm(Imm));
  load_trans load_trans_1 (.ReadData(ReadData), .LoadSel(LoadSel), .ReadDataTrans(ReadDataTrans));

  // Other names for the same wires on the sheet: clk = CLOCK; fetch_addr[31:0] = FETCH_ADDRESS;
  //   opcode[6:0] = INST[6:0]; rd[4:0] = INST[11:7]; INST (some bits) = {func7, func3}; rs1[4:0] = INST[19:15];
  //   rs2[4:0] = INST[24:20]

  // Notes on the sheet:
  //   Output
  //   Inputs/Outputs from run.circ. DO NOT MOVE THESE.
  //   Inputs
  //   Inputs/Outputs from run.circ. DO NOT MOVE THESE.
endmodule

module branchCompare (
  input  BrUn,
  input  [31:0] rs1,
  input  [31:0] rs2,
  output BrEq,
  output BrLt
);

  wire comparator_1_lt, comparator_2_lt;

  Comparator #(.width(32)) comparator_1 (.a(rs1), .b(rs2), .eq(BrEq), .lt(comparator_1_lt));  // open: gt
  Comparator #(.width(32), .mode("unsigned")) comparator_2 (.a(rs1), .b(rs2), .lt(comparator_2_lt));  // open: gt, eq
  Multiplexer #(.enable("false")) multiplexer_1 (.in0(comparator_1_lt), .in1(comparator_2_lt), .out(BrLt), .sel(BrUn));
endmodule

module control (
  input  [31:0] Instruction,
  input  BrEq,
  input  BrLt,
  output PCSel,
  output RegWEn,
  output [2:0] ImmSel,
  output BrUn,
  output ASel,
  output BSel,
  output [3:0] ALUSel,
  output MemRW,
  output [1:0] WBSel,
  output [2:0] LoadSel
);

  wire and_25_out, and_26_out, and_27_out, and_28_out, Bjump, comparator_1_eq, comparator_2_eq,
       comparator_3_eq, comparator_4_eq, comparator_5_eq, comparator_6_eq, comparator_7_eq, comparator_8_eq,
       comparator_9_eq, comparator_10_eq, comparator_11_eq, comparator_12_eq, comparator_19_eq,
       comparator_20_eq, comparator_21_eq, comparator_22_eq, comparator_23_eq, comparator_24_eq,
       comparator_25_eq, comparator_26_eq, comparator_27_eq, comparator_28_eq, comparator_29_eq,
       comparator_30_eq, comparator_32_eq, comparator_33_eq, comparator_34_eq, comparator_35_eq,
       comparator_36_eq, comparator_37_eq, comparator_38_eq, comparator_39_eq, comparator_41_eq,
       comparator_42_eq, comparator_43_eq, comparator_44_eq, comparator_45_eq, comparator_46_eq,
       comparator_47_eq, comparator_48_eq, comparator_49_eq, comparator_50_eq, comparator_51_eq,
       comparator_52_eq, isadd, isaddi, isauipc, isbeq, isbgeu, isblt, isbltu, isbne, isdiv, isdivu, isItype,
       isItype3, isjalr, islb, islbu, islh, islhu, islui, islw, ismul, ismulh, ismulhu, isor, isori, isremu,
       isRtype, isSBtype, issll, isslli, isslti, issrl, issrli, issub, isUJtype, isUtype, isxor, isxori,
       Jjump, not_1_out, not_2_out, or_1_out, or_2_out, or_3_out, or_5_out, or_6_out, or_7_out, or_10_out,
       or_15_out, WB_ALU1;
  wire [1:0] multiplexer_17_out, multiplexer_20_out;
  wire [2:0] multiplexer_16_out, multiplexer_18_out, multiplexer_19_out, multiplexer_23_out,
       multiplexer_24_out, multiplexer_25_out;
  wire [3:0] IRsel, multiplexer_1_out, multiplexer_2_out, multiplexer_3_out, multiplexer_4_out,
       multiplexer_5_out, multiplexer_6_out, multiplexer_7_out, multiplexer_8_out, multiplexer_9_out,
       multiplexer_10_out, multiplexer_11_out, multiplexer_12_out;

  or or_1 (or_1_out, isor, isori);
  Comparator #(.width(7)) comparator_1 (.a(Instruction[31:25]), .b({7{1'b0}}), .eq(comparator_1_eq));  // open: gt, lt
  Comparator #(.width(3)) comparator_2 (.a(Instruction[14:12]), .b(3'b000), .eq(comparator_2_eq));  // open: gt, lt
  Comparator #(.width(7)) comparator_3 (.a(Instruction[31:25]), .b(7'b0000001), .eq(comparator_3_eq));  // open: gt, lt
  Comparator #(.width(3)) comparator_4 (.a(Instruction[14:12]), .b(3'b000), .eq(comparator_4_eq));  // open: gt, lt
  Comparator #(.width(7)) comparator_5 (.a(Instruction[31:25]), .b(7'b0100000), .eq(comparator_5_eq));  // open: gt, lt
  Comparator #(.width(3)) comparator_6 (.a(Instruction[14:12]), .b(3'b000), .eq(comparator_6_eq));  // open: gt, lt
  Comparator #(.width(7)) comparator_7 (.a(Instruction[31:25]), .b({7{1'b0}}), .eq(comparator_7_eq));  // open: gt, lt
  Comparator #(.width(3)) comparator_8 (.a(Instruction[14:12]), .b(3'b001), .eq(comparator_8_eq));  // open: gt, lt
  Comparator #(.width(7)) comparator_9 (.a(Instruction[31:25]), .b(7'b0000001), .eq(comparator_9_eq));  // open: gt, lt
  Comparator #(.width(3)) comparator_10 (.a(Instruction[14:12]), .b(3'b001), .eq(comparator_10_eq));  // open: gt, lt
  Comparator #(.width(7)) comparator_11 (
    .a(Instruction[31:25]), .b(7'b0000001), .eq(comparator_11_eq));  // open: gt, lt
  Comparator #(.width(3)) comparator_12 (.a(Instruction[14:12]), .b(3'b011), .eq(comparator_12_eq));  // open: gt, lt
  Multiplexer #(.width(4), .enable("false")) multiplexer_1 (
    .in0(4'b0000), .in1(4'b0001), .out(multiplexer_1_out), .sel(or_1_out));
  Multiplexer #(.width(4), .enable("false")) multiplexer_2 (
    .in0(multiplexer_1_out), .in1(4'b0010), .out(multiplexer_2_out), .sel(or_2_out));
  or or_2 (or_2_out, isxor, isxori);
  and and_1 (isadd, comparator_1_eq, comparator_2_eq, isRtype);
  and and_2 (ismul, comparator_3_eq, comparator_4_eq, isRtype);
  and and_3 (issub, comparator_5_eq, comparator_6_eq, isRtype);
  and and_4 (issll, comparator_7_eq, comparator_8_eq, isRtype);
  and and_5 (ismulh, comparator_9_eq, comparator_10_eq, isRtype);
  and and_6 (ismulhu, comparator_11_eq, comparator_12_eq, isRtype);
  Multiplexer #(.width(4), .enable("false")) multiplexer_3 (
    .in0(multiplexer_2_out), .in1(4'b0011), .out(multiplexer_3_out), .sel(or_3_out));
  or or_3 (or_3_out, isadd, isaddi);
  Comparator #(.width(7)) comparator_13 (.a(Instruction[6:0]), .b(7'b0110011), .eq(isRtype));  // open: gt, lt
  Comparator #(.width(7)) comparator_14 (.a(Instruction[6:0]), .b(7'b0010011), .eq(isItype));  // open: gt, lt
  Comparator #(.width(7)) comparator_15 (.a(Instruction[6:0]), .b(7'b0110111), .eq(islui));  // open: gt, lt
  Multiplexer #(.width(4), .enable("false")) multiplexer_4 (
    .in0(multiplexer_3_out), .in1(4'b0100), .out(multiplexer_4_out), .sel(issub));
  Multiplexer #(.width(4), .enable("false")) multiplexer_5 (
    .in0(multiplexer_4_out), .in1(4'b0101), .out(multiplexer_5_out), .sel(ismul));
  Comparator #(.width(7)) comparator_16 (.a(Instruction[6:0]), .b(7'b0100011), .eq(MemRW));  // open: gt, lt
  Comparator #(.width(7)) comparator_17 (.a(Instruction[6:0]), .b(7'b0000011), .eq(isItype3));  // open: gt, lt
  Comparator #(.width(7)) comparator_18 (.a(Instruction[6:0]), .b(7'b0010111), .eq(isauipc));  // open: gt, lt
  Comparator #(.width(7)) comparator_19 (.a(Instruction[31:25]), .b({7{1'b0}}), .eq(comparator_19_eq));  // open: gt, lt
  Comparator #(.width(3)) comparator_20 (.a(Instruction[14:12]), .b(3'b100), .eq(comparator_20_eq));  // open: gt, lt
  Comparator #(.width(7)) comparator_21 (
    .a(Instruction[31:25]), .b(7'b0000001), .eq(comparator_21_eq));  // open: gt, lt
  Comparator #(.width(3)) comparator_22 (.a(Instruction[14:12]), .b(3'b100), .eq(comparator_22_eq));  // open: gt, lt
  Comparator #(.width(7)) comparator_23 (
    .a(Instruction[31:25]), .b(7'b0000001), .eq(comparator_23_eq));  // open: gt, lt
  Comparator #(.width(3)) comparator_24 (.a(Instruction[14:12]), .b(3'b101), .eq(comparator_24_eq));  // open: gt, lt
  Comparator #(.width(7)) comparator_25 (.a(Instruction[31:25]), .b({7{1'b0}}), .eq(comparator_25_eq));  // open: gt, lt
  Comparator #(.width(3)) comparator_26 (.a(Instruction[14:12]), .b(3'b101), .eq(comparator_26_eq));  // open: gt, lt
  Comparator #(.width(7)) comparator_27 (.a(Instruction[31:25]), .b({7{1'b0}}), .eq(comparator_27_eq));  // open: gt, lt
  Comparator #(.width(3)) comparator_28 (.a(Instruction[14:12]), .b(3'b110), .eq(comparator_28_eq));  // open: gt, lt
  Comparator #(.width(7)) comparator_29 (
    .a(Instruction[31:25]), .b(7'b0000001), .eq(comparator_29_eq));  // open: gt, lt
  Comparator #(.width(3)) comparator_30 (.a(Instruction[14:12]), .b(3'b111), .eq(comparator_30_eq));  // open: gt, lt
  Multiplexer #(.width(4), .enable("false")) multiplexer_6 (
    .in0(multiplexer_5_out), .in1(4'b0110), .out(multiplexer_6_out), .sel(ismulhu));
  Multiplexer #(.width(4), .enable("false")) multiplexer_7 (
    .in0(multiplexer_6_out), .in1(4'b0111), .out(multiplexer_7_out), .sel(ismulh));
  and and_7 (isxor, comparator_19_eq, comparator_20_eq, isRtype);
  and and_8 (isdiv, comparator_21_eq, comparator_22_eq, isRtype);
  and and_9 (isdivu, comparator_23_eq, comparator_24_eq, isRtype);
  and and_10 (issrl, comparator_25_eq, comparator_26_eq, isRtype);
  and and_11 (isor, comparator_27_eq, comparator_28_eq, isRtype);
  and and_12 (isremu, comparator_29_eq, comparator_30_eq, isRtype);
  Multiplexer #(.width(4), .enable("false")) multiplexer_8 (
    .in0(multiplexer_7_out), .in1(4'b1000), .out(multiplexer_8_out), .sel(isdivu));
  Multiplexer #(.width(4), .enable("false")) multiplexer_9 (
    .in0(multiplexer_8_out), .in1(4'b1001), .out(multiplexer_9_out), .sel(isdiv));
  Comparator #(.width(7)) comparator_31 (.a(Instruction[6:0]), .b(7'b1100011), .eq(isSBtype));  // open: gt, lt
  Multiplexer #(.width(4), .enable("false")) multiplexer_10 (
    .in0(multiplexer_9_out), .in1(4'b1010), .out(multiplexer_10_out), .sel(isremu));
  or or_4 (isUtype, isauipc, islui);
  Multiplexer #(.width(4), .enable("false")) multiplexer_11 (
    .in0(multiplexer_10_out), .in1(4'b1011), .out(multiplexer_11_out), .sel(or_5_out));
  or or_5 (or_5_out, issrl, issrli);
  Comparator #(.width(3)) comparator_32 (.a(Instruction[14:12]), .b(3'b000), .eq(comparator_32_eq));  // open: gt, lt
  Comparator #(.width(7)) comparator_33 (.a(Instruction[31:25]), .b({7{1'b0}}), .eq(comparator_33_eq));  // open: gt, lt
  Comparator #(.width(3)) comparator_34 (.a(Instruction[14:12]), .b(3'b001), .eq(comparator_34_eq));  // open: gt, lt
  Comparator #(.width(3)) comparator_35 (.a(Instruction[14:12]), .b(3'b010), .eq(comparator_35_eq));  // open: gt, lt
  Comparator #(.width(3)) comparator_36 (.a(Instruction[14:12]), .b(3'b100), .eq(comparator_36_eq));  // open: gt, lt
  Comparator #(.width(7)) comparator_37 (.a(Instruction[31:25]), .b({7{1'b0}}), .eq(comparator_37_eq));  // open: gt, lt
  Comparator #(.width(3)) comparator_38 (.a(Instruction[14:12]), .b(3'b101), .eq(comparator_38_eq));  // open: gt, lt
  Comparator #(.width(3)) comparator_39 (.a(Instruction[14:12]), .b(3'b110), .eq(comparator_39_eq));  // open: gt, lt
  Multiplexer #(.width(4), .enable("false")) multiplexer_12 (
    .in0(multiplexer_11_out), .in1(4'b1101), .out(multiplexer_12_out), .sel(isslti));
  Multiplexer #(.width(4), .enable("false")) multiplexer_13 (.in0(4'b0011), .in1(IRsel), .out(ALUSel), .sel(or_6_out));
  or or_6 (or_6_out, isRtype, isItype);
  or or_7 (or_7_out, isslli, issll);
  Comparator #(.width(7)) comparator_40 (.a(Instruction[6:0]), .b(7'b1101111), .eq(isUJtype));  // open: gt, lt
  Comparator #(.width(7)) comparator_41 (.a(Instruction[6:0]), .b(7'b1100111), .eq(comparator_41_eq));  // open: gt, lt
  Comparator #(.width(3)) comparator_42 (.a(Instruction[14:12]), .b(3'b000), .eq(comparator_42_eq));  // open: gt, lt
  and and_13 (isaddi, comparator_32_eq, isItype);
  and and_14 (isslli, comparator_33_eq, comparator_34_eq, isItype);
  and and_15 (isslti, comparator_35_eq, isItype);
  and and_16 (isxori, comparator_36_eq, isItype);
  and and_17 (issrli, comparator_37_eq, comparator_38_eq, isItype);
  and and_18 (isori, comparator_39_eq, isItype);
  Multiplexer #(.width(4), .enable("false")) multiplexer_14 (
    .in0(multiplexer_12_out), .in1(4'b1111), .out(IRsel), .sel(or_7_out));
  and and_19 (isjalr, comparator_41_eq, comparator_42_eq);
  Multiplexer #(.enable("false")) multiplexer_15 (.in0(1'b1), .in1(1'b0), .out(BSel), .sel(isRtype));
  Comparator #(.width(3)) comparator_43 (.a(Instruction[14:12]), .b(3'b000), .eq(comparator_43_eq));  // open: gt, lt
  Comparator #(.width(3)) comparator_44 (.a(Instruction[14:12]), .b(3'b100), .eq(comparator_44_eq));  // open: gt, lt
  Comparator #(.width(3)) comparator_45 (.a(Instruction[14:12]), .b(3'b110), .eq(comparator_45_eq));  // open: gt, lt
  Comparator #(.width(3)) comparator_46 (.a(Instruction[14:12]), .b(3'b001), .eq(comparator_46_eq));  // open: gt, lt
  Comparator #(.width(3)) comparator_47 (.a(Instruction[14:12]), .b(3'b111), .eq(comparator_47_eq));  // open: gt, lt
  Multiplexer #(.width(3), .enable("false")) multiplexer_16 (
    .in0(3'b000), .in1(3'b001), .out(multiplexer_16_out), .sel(MemRW));
  and and_20 (isbeq, comparator_43_eq, isSBtype);
  and and_21 (isblt, comparator_44_eq, isSBtype);
  and and_22 (isbltu, comparator_45_eq, isSBtype);
  and and_23 (isbne, comparator_46_eq, isSBtype);
  and and_24 (isbgeu, comparator_47_eq, isSBtype);
  or or_8 (WB_ALU1, isRtype, isauipc, isItype);
  Multiplexer #(.width(2), .enable("false")) multiplexer_17 (
    .in0(2'b00), .in1(2'b01), .out(multiplexer_17_out), .sel(WB_ALU1));
  Multiplexer #(.width(3), .enable("false")) multiplexer_18 (
    .in0(multiplexer_16_out), .in1(3'b010), .out(multiplexer_18_out), .sel(isSBtype));
  Multiplexer #(.width(3), .enable("false")) multiplexer_19 (
    .in0(multiplexer_18_out), .in1(3'b011), .out(multiplexer_19_out), .sel(isUtype));
  or or_9 (ASel, isauipc, isSBtype, isUJtype);
  not not_1 (not_1_out, BrLt);
  Multiplexer #(.width(2), .enable("false")) multiplexer_20 (
    .in0(multiplexer_17_out), .in1(2'b10), .out(multiplexer_20_out), .sel(Jjump));
  Multiplexer #(.width(3), .enable("false")) multiplexer_21 (
    .in0(multiplexer_19_out), .in1(3'b100), .out(ImmSel), .sel(isUJtype));
  and and_25 (and_25_out, BrEq, isbeq);
  and and_26 (and_26_out, isbne, not_2_out);
  not not_2 (not_2_out, BrEq);
  or or_10 (or_10_out, isblt, isbltu);
  and and_27 (and_27_out, or_10_out, BrLt);
  and and_28 (and_28_out, not_1_out, isbgeu);
  Multiplexer #(.width(2), .enable("false")) multiplexer_22 (
    .in0(multiplexer_20_out), .in1(2'b11), .out(WBSel), .sel(islui));
  or or_11 (Jjump, isjalr, isUJtype);
  or or_12 (BrUn, isbltu, isbgeu);
  or or_13 (Bjump, and_25_out, and_26_out, and_27_out, and_28_out);
  or or_14 (PCSel, Jjump, Bjump);
  Comparator #(.width(3)) comparator_48 (.a(Instruction[14:12]), .b(3'b000), .eq(comparator_48_eq));  // open: gt, lt
  Comparator #(.width(3)) comparator_49 (.a(Instruction[14:12]), .b(3'b001), .eq(comparator_49_eq));  // open: gt, lt
  Comparator #(.width(3)) comparator_50 (.a(Instruction[14:12]), .b(3'b010), .eq(comparator_50_eq));  // open: gt, lt
  Comparator #(.width(3)) comparator_51 (.a(Instruction[14:12]), .b(3'b100), .eq(comparator_51_eq));  // open: gt, lt
  Comparator #(.width(3)) comparator_52 (.a(Instruction[14:12]), .b(3'b101), .eq(comparator_52_eq));  // open: gt, lt
  and and_29 (islb, comparator_48_eq, isItype3);
  and and_30 (islh, comparator_49_eq, isItype3);
  and and_31 (islw, comparator_50_eq, isItype3);
  and and_32 (islbu, comparator_51_eq, isItype3);
  and and_33 (islhu, comparator_52_eq, isItype3);
  or or_15 (or_15_out, MemRW, isSBtype);
  Multiplexer #(.width(3), .enable("false")) multiplexer_23 (
    .in0(3'b000), .in1(3'b001), .out(multiplexer_23_out), .sel(islh));
  Multiplexer #(.width(3), .enable("false")) multiplexer_24 (
    .in0(multiplexer_23_out), .in1(3'b010), .out(multiplexer_24_out), .sel(islhu));
  not not_3 (RegWEn, or_15_out);
  Multiplexer #(.width(3), .enable("false")) multiplexer_25 (
    .in0(multiplexer_24_out), .in1(3'b011), .out(multiplexer_25_out), .sel(islb));
  Multiplexer #(.width(3), .enable("false")) multiplexer_26 (
    .in0(multiplexer_25_out), .in1(3'b100), .out(LoadSel), .sel(islbu));

  // Other names for the same wires on the sheet: Inst[31:0] = Instruction; opcode[6:0] = Instruction[6:0];
  //   rd[4:0] = Instruction[11:7]; func3[2:0] = Instruction[14:12]; rs1[4:0] = Instruction[19:15];
  //   rs2[4:0] = Instruction[24:20]; func7[6:0] = Instruction[31:25]; isStype = MemRW

  // Notes on the sheet:
  //   decode
  //   ALUsel
  //   TypeJudge
  //   Bsel
  //   Asel
  //   IMMsel
  //   PCsel
  //   WBsel
  //   MemRW
  //   BrUn
  //   LoadSel
  //   RegWEn
endmodule

module immGen (
  input  [31:0] Instruction,
  input  [2:0] ImmSel,
  output [31:0] imm
);

  wire [31:0] imm_I, imm_S, imm_SB, imm_UJ;

  assign imm_I = {{20{Instruction[31]}}, Instruction[31:20]};  // Bit_Extender bit_extender_1
  assign imm_S = {{20{Instruction[31]}}, {Instruction[31:25], Instruction[11:7]}};  // Bit_Extender bit_extender_2
  assign imm_SB = {{19{Instruction[31]}}, {Instruction[31], Instruction[7], Instruction[30:25], Instruction[11:8], 1'b0}};  // Bit_Extender bit_extender_3
  assign imm_UJ = {{11{Instruction[31]}}, {Instruction[31], Instruction[19:12], Instruction[20], Instruction[30:21], 1'b0}};  // Bit_Extender bit_extender_4
  Multiplexer #(.select(3), .width(32), .enable("false")) multiplexer_1 (
    .in0(imm_I), .in1(imm_S), .in2(imm_SB), .in3({Instruction[31:12], {12{1'b0}}}), .in4(imm_UJ), .out(imm),
    .sel(ImmSel));  // open: in5, in6, in7

  // Other names for the same wires on the sheet: INST[31:0] = Instruction; imm_U[31:12] = Instruction[31:12]
endmodule

module load_trans (
  input  [31:0] ReadData,
  input  [2:0] LoadSel,
  output [31:0] ReadDataTrans
);

  wire [31:0] LB, LBU, LH, LHU;

  assign LH = {{16{ReadData[15]}}, ReadData[15:0]};  // Bit_Extender bit_extender_1
  assign LHU = {{16{1'b0}}, ReadData[15:0]};  // Bit_Extender bit_extender_2
  assign LB = {{24{ReadData[7]}}, ReadData[7:0]};  // Bit_Extender bit_extender_3
  assign LBU = {{24{1'b0}}, ReadData[7:0]};  // Bit_Extender bit_extender_4
  Multiplexer #(.select(3), .width(32), .enable("false")) multiplexer_1 (
    .in0(ReadData), .in1(LH), .in2(LHU), .in3(LB), .in4(LBU), .out(ReadDataTrans), .sel(LoadSel));  // open: in5, in6, in7
endmodule
