// Logisim project regfile.circ as structural Verilog: 1 circuit, main circuit main
module main (
  input  [4:0] rs1,
  input  [4:0] rs2,
  input  [4:0] rd,
  input  [31:0] Write_Data,
  input  RegWEn,
  input  clk,
  output [31:0] ra,
  output [31:0] sp,
  output [31:0] t0,
  output [31:0] t1,
  output [31:0] t2,
  output [31:0] s0,
  output [31:0] s1,
  output [31:0] a0,
  output [31:0] Read_Data_1,
  output [31:0] Read_Data_2
);

  wire a0_mod, ra_mod, s0_mod, s1_mod, sp_mod, t0_mod, t1_mod, t2_mod;
  wire [31:0] a0_data, ra_data, s0_data, s1_data, sp_data, t0_data, t1_data, t2_data, x0;

  Demultiplexer #(.select(5), .enable("false")) demultiplexer_1 (
    .out1(ra_mod), .out2(sp_mod), .out5(t0_mod), .out6(t1_mod), .out7(t2_mod), .out8(s0_mod), .out9(s1_mod),
    .out10(a0_mod), .in(RegWEn), .sel(rd));  // open: out0, out3, out4, out11, out12, out13, out14, out15, out16, out17, out18, out19, out20, out21, out22, out23, out24, out25, out26, out27, out28, out29, out30, out31
  Register #(.width(32)) register_1 (.D(ra_data), .en(ra_mod), .clk(clk), .Q(ra));  // open: clr
  Register #(.width(32)) register_2 (.D(t1_data), .en(t1_mod), .clk(clk), .Q(t1));  // open: clr
  Register #(.width(32)) register_3 (.D(s1_data), .en(s1_mod), .clk(clk), .Q(s1));  // open: clr
  Demultiplexer #(.select(5), .width(32), .enable("false")) demultiplexer_2 (
    .out1(ra_data), .out2(sp_data), .out5(t0_data), .out6(t1_data), .out7(t2_data), .out8(s0_data),
    .out9(s1_data), .out10(a0_data), .in(Write_Data), .sel(rd));  // open: out0, out3, out4, out11, out12, out13, out14, out15, out16, out17, out18, out19, out20, out21, out22, out23, out24, out25, out26, out27, out28, out29, out30, out31
  Register #(.width(32)) register_4 (.D(sp_data), .en(sp_mod), .clk(clk), .Q(sp));  // open: clr
  Register #(.width(32)) register_5 (.D(t2_data), .en(t2_mod), .clk(clk), .Q(t2));  // open: clr
  Register #(.width(32)) register_6 (.D(a0_data), .en(a0_mod), .clk(clk), .Q(a0));  // open: clr
  Multiplexer #(.select(5), .width(32), .enable("false")) multiplexer_1 (
    .in0(x0), .in1(ra), .in2(sp), .in5(t0), .in6(t1), .in7(t2), .in8(s0), .in9(s1), .in10(a0),
    .out(Read_Data_1), .sel(rs1));  // open: in3, in4, in11, in12, in13, in14, in15, in16, in17, in18, in19, in20, in21, in22, in23, in24, in25, in26, in27, in28, in29, in30, in31
  Register #(.width(32)) register_7 (.D(t0_data), .en(t0_mod), .clk(clk), .Q(t0));  // open: clr
  Register #(.width(32)) register_8 (.D(s0_data), .en(s0_mod), .clk(clk), .Q(s0));  // open: clr
  Register #(.width(32)) register_9 (.D({32{1'b0}}), .clk(clk), .Q(x0));  // open: en, clr
  Multiplexer #(.select(5), .width(32), .enable("false")) multiplexer_2 (
    .in0(x0), .in1(ra), .in2(sp), .in5(t0), .in6(t1), .in7(t2), .in8(s0), .in9(s1), .in10(a0),
    .out(Read_Data_2), .sel(rs2));  // open: in3, in4, in11, in12, in13, in14, in15, in16, in17, in18, in19, in20, in21, in22, in23, in24, in25, in26, in27, in28, in29, in30, in31

  // Other names for the same wires on the sheet: read_data1[31:0] = Read_Data_1; read_data2[31:0] = Read_Data_2;
  //   read_reg1[4:0] = rs1; read_reg2[4:0] = rs2; write_en = RegWEn; write_reg[4:0] = rd

  // Notes on the sheet:
  //   INPUTS to your circuit
  //   DON'T CHANGE THE LOCATIONS OF THE INPUTS AND OUTPUTS!
  //   These are DEBUG/TEST outputs from your circuit.
  //   OUTPUTS from your circuit
endmodule
